# Fritzing sketch timer (saved by Fritzing 0.9.2b)
circuit board: 11.4441cm x 6.95677cm
breadboards: 1

parts:
  U11 = ESP8266 WiFi Module [part_number=ESP8266]
  U12 = RELAY [package=relay-t9a]
  U13 = Voltage Regulator - 3.3V [package="TO220 [THT]"]
  R1 = Resistor [tolerance=±5% resistance=1k package="0603 [SMD]"]
  Load = Photocell (LDR) [package=THT]
  HOT = Header 1 [package=1x01_offset]
  NEUTRAL = Header 1 [package=1x01_offset]
  R2 = Resistor [tolerance=±5% resistance=1k package="0603 [SMD]"]
  Load1 = Photocell (LDR) [package=THT]
  NEUTRAL1 = Header 1 [package=1x01_offset]
  HOT1 = Header 1 [package=1x01_offset]
  U14 = RELAY [package=relay-t9a]
  U15 = Voltage Regulator - 3.3V [package="TO220 [THT]"]
  U16 = ESP8266 WiFi Module [part_number=ESP8266]
  Q1 = TRANSISTOR_NPN [package=to-92-ammo]
  R3 = Resistor [tolerance=±5% resistance=1k package="0603 [SMD]"]
  C3 = Ceramic Capacitor [capacitance=0.1µF package="1206 [SMD, multilayer]"]
  C4 = Capacitor Polarized [part_number=1000μF package=panasonic_h13]
  C5 = Ceramic Capacitor [capacitance=0.1µF package="1206 [SMD, multilayer]"]
  C6 = Capacitor Polarized [part_number=1000μF package=panasonic_h13]

nets:
  N1: U11.VCC, U11.RST, U11.CH_PD, U13.output_voltage, C5.1, C6.+
  N2: U11.GPIO_2, R3.Pin_0
  GND: U11.GND, U12.COIL2, U13.GND, U14.COIL2, U15.GND, U16.GND, Q1.E, C3.0, C4.-, C5.0, C6.-
  N3: U12.COIL1, R1.Pin_0, Q1.C
  N4: U12.MAIN, HOT.1
  N5: U12.NO, Load.pin_0
  5V: U13.input_voltage, R1.Pin_1, U15.input_voltage
  N6: Load.pin_1, NEUTRAL.1
  N7: R2.Pin_0, U14.COIL1, U16.GPIO_2
  N8: R2.Pin_1, U15.output_voltage, U16.VCC, U16.RST, U16.CH_PD, C3.1, C4.+
  N9: Load1.pin_0, U14.NO
  N10: Load1.pin_1, NEUTRAL1.1
  N11: HOT1.1, U14.MAIN
  N12: Q1.B, R3.Pin_1

custom parts:
  ESP8266 WiFi Module: Generic WiFi Module based on the ESP8266 with onboard PCB antenna and UART communications
